# Fritzing sketch lab05 (saved by Fritzing 0.9.2b)
breadboards: 1

parts:
  BeagleBone1 = BeagleBone Black
  R1 = Resistor [tolerance=±5% resistance=220 package="1206 [SMD]"]
  R2 = Resistor [tolerance=±5% resistance=220 package="1206 [SMD]"]
  Part1 = SRF05 Ultrasonic Rangefinder

nets:
  N1: BeagleBone1.no_name_yet#1, BeagleBone1.no_name_yet#204, R1.Pin_0, Part1.GND
  N2: BeagleBone1.no_name_yet#7, Part1.VCC
  N3: BeagleBone1.no_name_yet#16, BeagleBone1.no_name_yet#206, Part1.Trig
  N4: BeagleBone1.no_name_yet#41, R1.Pin_1, R2.Pin_0
  N5: BeagleBone1.no_name_yet#205, R2.Pin_1, Part1.Echo

custom parts:
  BeagleBone Black: BeagleBone Black rev. A5B
